// Logisim project SP1_COMPUTER.circ as structural Verilog
module DecoderInstruct (
  input  in_1,
  input  in_2,
  input  in_3,
  input  in_4,
  output out_5,
  output out_6,
  output out_7,
  output out_8,
  output out_9
);

  wire not_1_out, not_2_out, not_3_out, not_4_out;

  not not_1 (not_1_out, in_1);
  not not_2 (not_2_out, in_2);
  not not_3 (not_3_out, in_4);
  not not_4 (not_4_out, in_3);
  and and_1 (out_5, not_3_out, not_4_out, not_2_out, not_1_out);
  and and_2 (out_6, in_4, not_4_out, not_2_out, not_1_out);
  and and_3 (out_7, not_3_out, in_3, not_2_out, not_1_out);
  and and_4 (out_8, in_4, in_3, not_2_out, not_1_out);
  nand nand_1 (out_9, in_4, in_3, in_2, in_1);

  // Notes on the sheet:
  //   LDA
  //   ADD
  //   SUB
  //   OUT
  //   \HLT
endmodule

module DringCounter (
  input  CLK,
  input  nCLR,
  output T1,
  output T2,
  output T3,
  output T4,
  output T5,
  output T6
);

  wire not_1_out, not_2_out, not_3_out, not_4_out, not_5_out, not_6_out, not_7_out, not_8_out, not_9_out,
       not_10_out, not_11_out, not_12_out;

  not not_1 (not_1_out, CLK);
  not not_2 (not_2_out, nCLR);
  D_Flip_Flop d_ff_1 (.clk(not_1_out), .D(T6), .Q(T1), .preset(not_2_out));  // open: Qn, en, reset
  not not_3 (not_3_out, CLK);
  D_Flip_Flop d_ff_2 (.clk(not_3_out), .D(T1), .Q(T2), .reset(not_4_out));  // open: Qn, preset, en
  not not_4 (not_4_out, nCLR);
  D_Flip_Flop d_ff_3 (.clk(not_5_out), .D(T2), .Q(T3), .reset(not_6_out));  // open: Qn, preset, en
  not not_5 (not_5_out, CLK);
  not not_6 (not_6_out, nCLR);
  not not_7 (not_7_out, CLK);
  not not_8 (not_8_out, CLK);
  D_Flip_Flop d_ff_4 (.clk(not_7_out), .D(T3), .Q(T4), .reset(not_9_out));  // open: Qn, preset, en
  not not_9 (not_9_out, nCLR);
  D_Flip_Flop d_ff_5 (.clk(not_8_out), .D(T4), .Q(T5), .reset(not_10_out));  // open: Qn, preset, en
  not not_10 (not_10_out, nCLR);
  D_Flip_Flop d_ff_6 (.clk(not_11_out), .D(T5), .Q(T6), .reset(not_12_out));  // open: Qn, preset, en
  not not_11 (not_11_out, CLK);
  not not_12 (not_12_out, nCLR);
endmodule

module ControlMatrix (
  input  in_1,
  input  in_2,
  input  I4,
  input  I3,
  input  I2,
  input  I1,
  output out_7,
  output Cp,
  output Ep,
  output nLm,
  output nCe,
  output nLi,
  output nEi,
  output nLa,
  output Ea,
  output Su,
  output Eu,
  output nLb,
  output nLo
);

  wire c39_1_out_9, c39_1_out_10, c39_1_out_11, c39_1_out_12, c39_2_out_9, c39_2_out_10, c39_2_out_11,
       c39_2_out_12, c39_3_out_9, c39_3_out_10, c39_3_out_11, c39_3_out_12, c39_4_out_9, c39_4_out_10,
       c39_4_out_11, c39_4_out_12, c43_1_out_7, c43_1_out_8, c46_1_out_6, decoderinstruct_1_out_5,
       decoderinstruct_1_out_6, decoderinstruct_1_out_7, decoderinstruct_1_out_8, dringcounter_1_t3,
       dringcounter_1_t4, dringcounter_1_t5, dringcounter_1_t6, not_1_out, not_2_out;

  DecoderInstruct decoderinstruct_1 (
    .out_5(decoderinstruct_1_out_5), .out_6(decoderinstruct_1_out_6), .out_7(decoderinstruct_1_out_7),
    .out_8(decoderinstruct_1_out_8), .out_9(out_7), .in_1(I4), .in_2(I3), .in_3(I2), .in_4(I1));
  DringCounter dringcounter_1 (
    .CLK(in_1), .nCLR(in_2), .T1(Ep), .T2(Cp), .T3(dringcounter_1_t3), .T4(dringcounter_1_t4),
    .T5(dringcounter_1_t5), .T6(dringcounter_1_t6));
  not not_1 (not_1_out, Ep);
  C39 c39_1 (
    .in_1(decoderinstruct_1_out_5), .in_2(dringcounter_1_t4), .in_3(decoderinstruct_1_out_6),
    .in_4(dringcounter_1_t4), .in_5(decoderinstruct_1_out_7), .in_6(dringcounter_1_t4),
    .in_7(decoderinstruct_1_out_5), .in_8(dringcounter_1_t3), .out_9(c39_1_out_9), .out_10(c39_1_out_10),
    .out_11(c39_1_out_11), .out_12(c39_1_out_12));
  not not_2 (not_2_out, dringcounter_1_t3);
  C44 C44 (
    .in_1(not_1_out), .in_2(c39_1_out_9), .in_3(c39_1_out_10), .in_4(c39_1_out_11), .in_5(not_2_out),
    .in_6(c39_1_out_12), .in_7(c39_2_out_9), .in_8(c39_2_out_10), .out_9(nLm), .out_10(nCe));
  C39 c39_2 (
    .in_1(decoderinstruct_1_out_6), .in_2(dringcounter_1_t3), .in_3(decoderinstruct_1_out_7),
    .in_4(dringcounter_1_t5), .in_5(decoderinstruct_1_out_5), .in_6(dringcounter_1_t4),
    .in_7(decoderinstruct_1_out_6), .in_8(dringcounter_1_t4), .out_9(c39_2_out_9), .out_10(c39_2_out_10),
    .out_11(c39_2_out_11), .out_12(c39_2_out_12));
  not not_3 (nLi, dringcounter_1_t3);
  C45 c45_1 (
    .in_1(c39_2_out_11), .in_2(c39_2_out_12), .in_3(c39_3_out_9), .in_4(c39_3_out_10), .in_5(c39_3_out_11),
    .in_6(c39_3_out_12), .out_7(nEi), .out_8(nLa));
  C39 c39_3 (
    .in_1(decoderinstruct_1_out_7), .in_2(dringcounter_1_t4), .in_3(decoderinstruct_1_out_5),
    .in_4(dringcounter_1_t5), .in_5(decoderinstruct_1_out_6), .in_6(dringcounter_1_t6),
    .in_7(decoderinstruct_1_out_7), .in_8(dringcounter_1_t6), .out_9(c39_3_out_9), .out_10(c39_3_out_10),
    .out_11(c39_3_out_11), .out_12(c39_3_out_12));
  not not_4 (Ea, c39_4_out_9);
  C39 c39_4 (
    .in_1(decoderinstruct_1_out_8), .in_2(dringcounter_1_t4), .in_3(decoderinstruct_1_out_7),
    .in_4(dringcounter_1_t6), .in_5(decoderinstruct_1_out_6), .in_6(dringcounter_1_t6),
    .in_7(decoderinstruct_1_out_7), .in_8(dringcounter_1_t6), .out_9(c39_4_out_9), .out_10(c39_4_out_10),
    .out_11(c39_4_out_11), .out_12(c39_4_out_12));
  not not_5 (Su, c39_4_out_10);
  C46 c46_1 (
    .in_1(c39_4_out_11), .in_2(c39_4_out_12), .in_3(c43_1_out_7), .in_4(c43_1_out_8), .out_5(Eu),
    .out_6(c46_1_out_6));
  not not_6 (nLb, c46_1_out_6);
  C43 c43_1 (
    .in_1(decoderinstruct_1_out_6), .in_2(dringcounter_1_t5), .in_3(decoderinstruct_1_out_7),
    .in_4(dringcounter_1_t5), .in_5(decoderinstruct_1_out_8), .in_6(dringcounter_1_t4), .out_7(c43_1_out_7),
    .out_8(c43_1_out_8), .out_9(nLo));

  // Notes on the sheet:
  //   CONTROL MATRIX
  //   C39
  //   C40
  //   C45
  //   C41
  //   C42
  //   C46
  //   C43
endmodule

module C39 (
  input  in_1,
  input  in_2,
  input  in_3,
  input  in_4,
  input  in_5,
  input  in_6,
  input  in_7,
  input  in_8,
  output out_9,
  output out_10,
  output out_11,
  output out_12
);

  nand nand_1 (out_9, in_1, in_2);
  nand nand_2 (out_10, in_3, in_4);
  nand nand_3 (out_11, in_5, in_6);
  nand nand_4 (out_12, in_7, in_8);
endmodule

module C43 (
  input  in_1,
  input  in_2,
  input  in_3,
  input  in_4,
  input  in_5,
  input  in_6,
  output out_7,
  output out_8,
  output out_9
);

  nand nand_1 (out_7, in_1, in_2);
  nand nand_2 (out_8, in_3, in_4);
  nand nand_3 (out_9, in_5, in_6);
endmodule

module SAP_ARC (
  input  in_1,
  input  in_2,
  input  in_3,
  input  in_4,
  input  in_5
);

  wire ir_register_1_out_13, ir_register_1_out_14, ir_register_1_out_15, ir_register_1_out_16,
       ir_register_1_out_17, ir_register_1_out_18, ir_register_1_out_19, ir_register_1_out_20, PC__1, PC__2,
       PC__3, PC__4, W_BUS_a1, W_BUS_a2, W_BUS_a3, W_BUS_a4;

  IR_REGISTER ir_register_1 (
    .out_13(ir_register_1_out_13), .out_14(ir_register_1_out_14), .out_15(ir_register_1_out_15),
    .out_16(ir_register_1_out_16), .out_17(ir_register_1_out_17), .out_18(ir_register_1_out_18),
    .out_19(ir_register_1_out_19), .out_20(ir_register_1_out_20));  // open: CLR, nEi, in_9, in_12, in_1, in_2, in_3, in_4, in_5, in_6, in_7, in_8
  ProgramCounter PC (._4(PC__4), ._3(PC__3), ._2(PC__2), ._1(PC__1));  // open: Cp, nCLK, nCLR, Ep
  MAR mar_1 (
    .A0(in_1), .A1(in_2), .A2(in_3), .A3(in_4), .PROG(in_5), .in_1(W_BUS_a4), .in_2(W_BUS_a3),
    .in_3(W_BUS_a2), .in_4(W_BUS_a1));  // open: in_5, in_6, A3_2, A2_2, A1_2, A0_2
  ControlMatrix controlmatrix_1 (
    .I4(ir_register_1_out_13), .I3(ir_register_1_out_14), .I2(ir_register_1_out_15), .I1(ir_register_1_out_16));  // open: in_1, in_2, out_7, Cp, Ep, nLm, nCe, nLi, nEi, nLa, Ea, Su, Eu, nLb, nLo
  W_BUS W_BUS (
    .PC1(PC__1), .PC2(PC__2), .PC3(PC__3), .PC4(PC__4), .A4(W_BUS_a4), .A3(W_BUS_a3), .A2(W_BUS_a2),
    .A1(W_BUS_a1), .D1(ir_register_1_out_20), .D2(ir_register_1_out_19), .D3(ir_register_1_out_18),
    .D4(ir_register_1_out_17));

  // Notes on the sheet:
  //   MAR
  //   CONTROL MTX
  //   IR
endmodule

module ProgramCounter (
  input  Cp,
  input  nCLK,
  input  nCLR,
  input  Ep,
  output _4,
  output _3,
  output _2,
  output _1
);

  wire j_k_ff_1_q, j_k_ff_2_q, j_k_ff_3_q, j_k_ff_4_q, not_1_out, not_2_out, not_3_out, not_4_out, not_5_out,
       not_6_out, not_7_out, not_8_out;

  J_K_Flip_Flop j_k_ff_1 (.J(Cp), .clk(not_1_out), .K(Cp), .Q(j_k_ff_1_q), .reset(not_2_out));  // open: Qn, preset, en
  not not_1 (not_1_out, nCLK);
  not not_2 (not_2_out, nCLR);
  not not_3 (not_3_out, j_k_ff_1_q);
  assign _1 = Ep ? j_k_ff_1_q : 1'bz;  // Controlled_Buffer controlled_buffer_1
  not not_4 (not_4_out, j_k_ff_2_q);
  J_K_Flip_Flop j_k_ff_2 (.J(Cp), .clk(not_3_out), .K(Cp), .Q(j_k_ff_2_q), .reset(not_5_out));  // open: Qn, preset, en
  not not_5 (not_5_out, nCLR);
  assign _2 = Ep ? j_k_ff_2_q : 1'bz;  // Controlled_Buffer controlled_buffer_2
  J_K_Flip_Flop j_k_ff_3 (.J(Cp), .clk(not_4_out), .K(Cp), .Q(j_k_ff_3_q), .reset(not_6_out));  // open: Qn, preset, en
  not not_6 (not_6_out, nCLR);
  assign _3 = Ep ? j_k_ff_3_q : 1'bz;  // Controlled_Buffer controlled_buffer_3
  not not_7 (not_7_out, j_k_ff_3_q);
  not not_8 (not_8_out, nCLR);
  J_K_Flip_Flop j_k_ff_4 (.J(Cp), .clk(not_7_out), .K(Cp), .Q(j_k_ff_4_q), .reset(not_8_out));  // open: Qn, preset, en
  assign _4 = Ep ? j_k_ff_4_q : 1'bz;  // Controlled_Buffer controlled_buffer_4
endmodule

module C44 (
  input  in_1,
  input  in_2,
  input  in_3,
  input  in_4,
  input  in_5,
  input  in_6,
  input  in_7,
  input  in_8,
  output out_9,
  output out_10
);

  wire not_1_out, not_2_out, not_3_out, not_4_out, not_5_out, not_6_out, not_7_out, not_8_out;

  not not_1 (not_1_out, in_2);
  not not_2 (not_2_out, in_3);
  not not_3 (not_3_out, in_1);
  nor nor_1 (out_9, not_3_out, not_1_out, not_2_out, not_4_out);
  not not_4 (not_4_out, in_4);
  not not_5 (not_5_out, in_5);
  not not_6 (not_6_out, in_7);
  not not_7 (not_7_out, in_6);
  not not_8 (not_8_out, in_8);
  nor nor_2 (out_10, not_5_out, not_7_out, not_6_out, not_8_out);
endmodule

module C45 (
  input  in_1,
  input  in_2,
  input  in_3,
  input  in_4,
  input  in_5,
  input  in_6,
  output out_7,
  output out_8
);

  wire not_1_out, not_2_out, not_3_out, not_4_out, not_5_out, not_6_out;

  not not_1 (not_1_out, in_2);
  not not_2 (not_2_out, in_1);
  nor nor_1 (out_7, not_2_out, not_1_out, not_3_out);
  not not_3 (not_3_out, in_3);
  not not_4 (not_4_out, in_4);
  not not_5 (not_5_out, in_5);
  nor nor_2 (out_8, not_4_out, not_5_out, not_6_out);
  not not_6 (not_6_out, in_6);
endmodule

module C46 (
  input  in_1,
  input  in_2,
  input  in_3,
  input  in_4,
  output out_5,
  output out_6
);

  wire not_1_out, not_2_out, not_3_out, not_4_out;

  not not_1 (not_1_out, in_1);
  or or_1 (out_5, not_1_out, not_2_out);
  not not_2 (not_2_out, in_2);
  not not_3 (not_3_out, in_3);
  not not_4 (not_4_out, in_4);
  or or_2 (out_6, not_3_out, not_4_out);
endmodule

module BufferRegister (
  input  X0,
  input  X1,
  input  X2,
  input  X3,
  input  LOAD,
  input  CLK,
  input  CLR,
  input  ENABLE,
  output D0,
  output D1,
  output D2,
  output D3
);

  wire and_1_out, and_2_out, and_3_out, and_4_out, and_5_out, and_6_out, and_7_out, and_8_out, d_ff_1_q,
       d_ff_2_q, d_ff_3_q, d_ff_4_q, not_1_out, or_1_out, or_2_out, or_3_out, or_4_out;

  not not_1 (not_1_out, LOAD);
  and and_1 (and_1_out, LOAD, X0);
  and and_2 (and_2_out, not_1_out, d_ff_1_q);
  or or_1 (or_1_out, and_1_out, and_2_out);
  and and_3 (and_3_out, LOAD, X1);
  or or_2 (or_2_out, and_3_out, and_4_out);
  D_Flip_Flop d_ff_1 (.clk(CLK), .D(or_1_out), .Q(d_ff_1_q), .reset(CLR));  // open: Qn, preset, en
  assign D0 = ENABLE ? d_ff_1_q : 1'bz;  // Controlled_Buffer controlled_buffer_1
  and and_4 (and_4_out, not_1_out, d_ff_2_q);
  and and_5 (and_5_out, LOAD, X2);
  D_Flip_Flop d_ff_2 (.clk(CLK), .D(or_2_out), .Q(d_ff_2_q), .reset(CLR));  // open: Qn, preset, en
  assign D1 = ENABLE ? d_ff_2_q : 1'bz;  // Controlled_Buffer controlled_buffer_2
  and and_6 (and_6_out, not_1_out, d_ff_3_q);
  or or_3 (or_3_out, and_5_out, and_6_out);
  D_Flip_Flop d_ff_3 (.clk(CLK), .D(or_3_out), .Q(d_ff_3_q), .reset(CLR));  // open: Qn, preset, en
  assign D2 = ENABLE ? d_ff_3_q : 1'bz;  // Controlled_Buffer controlled_buffer_3
  and and_7 (and_7_out, not_1_out, d_ff_4_q);
  and and_8 (and_8_out, LOAD, X3);
  or or_4 (or_4_out, and_8_out, and_7_out);
  D_Flip_Flop d_ff_4 (.clk(CLK), .D(or_4_out), .Q(d_ff_4_q), .reset(CLR));  // open: Qn, preset, en
  assign D3 = ENABLE ? d_ff_4_q : 1'bz;  // Controlled_Buffer controlled_buffer_4
endmodule

module MAR (
  input  in_1,
  input  in_2,
  input  in_3,
  input  in_4,
  input  in_5,
  input  in_6,
  input  A0,
  input  A1,
  input  A2,
  input  A3,
  input  PROG,
  output A3_2,
  output A2_2,
  output A1_2,
  output A0_2
);

  wire bufferregister_1_d0, bufferregister_1_d1, bufferregister_1_d2, bufferregister_1_d3,
       n2to1multiplexer_1_out_10, n2to1multiplexer_1_out_11, n2to1multiplexer_1_out_12,
       n2to1multiplexer_1_out_13, not_1_out;

  BufferRegister bufferregister_1 (
    .LOAD(in_5), .CLK(in_6), .CLR(not_1_out), .ENABLE(1'b1), .X0(in_4), .X1(in_3), .X2(in_2), .X3(in_1),
    .D0(bufferregister_1_d0), .D1(bufferregister_1_d1), .D2(bufferregister_1_d2), .D3(bufferregister_1_d3));
  not not_1 (not_1_out, 1'b1);
  _2TO1MULTIPLEXER u_2to1multiplexer_1 (
    .in_9(PROG), .in_1(A3), .in_2(bufferregister_1_d3), .in_3(A2), .in_4(bufferregister_1_d2), .in_5(A1),
    .in_6(bufferregister_1_d1), .in_7(A0), .in_8(bufferregister_1_d0), .out_10(n2to1multiplexer_1_out_10),
    .out_11(n2to1multiplexer_1_out_11), .out_12(n2to1multiplexer_1_out_12), .out_13(n2to1multiplexer_1_out_13));
  not not_2 (A3_2, n2to1multiplexer_1_out_10);
  not not_3 (A2_2, n2to1multiplexer_1_out_11);
  not not_4 (A1_2, n2to1multiplexer_1_out_12);
  not not_5 (A0_2, n2to1multiplexer_1_out_13);
endmodule

module _2TO1MULTIPLEXER (
  input  in_1,
  input  in_2,
  input  in_3,
  input  in_4,
  input  in_5,
  input  in_6,
  input  in_7,
  input  in_8,
  input  in_9,
  output out_10,
  output out_11,
  output out_12,
  output out_13
);

  wire and_1_out, and_2_out, and_3_out, and_4_out, and_5_out, and_6_out, and_7_out, and_8_out, and_9_out,
       and_10_out, not_1_out, not_2_out, not_3_out, not_4_out, not_5_out;

  not not_1 (not_1_out, in_9);
  not not_2 (not_2_out, not_1_out);
  and and_1 (and_1_out, not_2_out, not_5_out);
  not not_3 (not_3_out, 1'b0);
  not not_4 (not_4_out, in_9);
  not not_5 (not_5_out, 1'b0);
  and and_2 (and_2_out, not_4_out, not_3_out);
  and and_3 (and_3_out, and_1_out, in_1);
  nor nor_1 (out_10, and_3_out, and_4_out);
  and and_4 (and_4_out, and_2_out, in_2);
  and and_5 (and_5_out, and_1_out, in_3);
  and and_6 (and_6_out, and_2_out, in_4);
  nor nor_2 (out_11, and_5_out, and_6_out);
  and and_7 (and_7_out, and_1_out, in_5);
  nor nor_3 (out_12, and_7_out, and_9_out);
  and and_8 (and_8_out, and_1_out, in_7);
  and and_9 (and_9_out, and_2_out, in_6);
  and and_10 (and_10_out, and_2_out, in_8);
  nor nor_4 (out_13, and_8_out, and_10_out);
endmodule

module IR_REGISTER (
  input  in_1,
  input  in_2,
  input  in_3,
  input  in_4,
  input  in_5,
  input  in_6,
  input  in_7,
  input  in_8,
  input  in_9,
  input  CLR,
  input  nEi,
  input  in_12,
  output out_13,
  output out_14,
  output out_15,
  output out_16,
  output out_17,
  output out_18,
  output out_19,
  output out_20
);

  wire not_1_out, not_2_out, not_3_out;

  BufferRegister bufferregister_1 (
    .LOAD(not_1_out), .CLK(in_12), .CLR(CLR), .ENABLE(1'b1), .X0(in_4), .X1(in_3), .X2(in_2), .X3(in_1),
    .D0(out_16), .D1(out_15), .D2(out_14), .D3(out_13));
  not not_1 (not_1_out, in_9);
  BufferRegister bufferregister_2 (
    .LOAD(not_3_out), .CLK(in_12), .CLR(1'b0), .ENABLE(not_2_out), .X0(in_8), .X1(in_7), .X2(in_6),
    .X3(in_5), .D0(out_20), .D1(out_19), .D2(out_18), .D3(out_17));
  not not_2 (not_2_out, nEi);
  not not_3 (not_3_out, in_9);
endmodule

module W_BUS (
  input  PC1,
  input  PC2,
  input  PC3,
  input  PC4,
  output A4,
  output A3,
  output A2,
  output A1,
  output D1,
  output D2,
  output D3,
  output D4
);


  assign A1 = PC1;
  assign A2 = PC2;
  assign A3 = PC3;
  assign A4 = PC4;
  assign D1 = PC1;
  assign D2 = PC2;
  assign D3 = PC3;
  assign D4 = PC4;
  // also tied to GND on the sheet: {PC3, PC4, PC1, PC2}

  // Notes on the sheet:
  //   PC DATA
endmodule

module RAM_MEMORY (
  input  [3:0] in_1,
  input  [3:0] in_2,
  input  in_3,
  input  in_4,
  input  in_5,
  input  in_6,
  output [3:0] out_7
);

  RAM #(.addrWidth(4), .dataWidth(4), .bus("asynch")) ram_1 (
    .addr(in_1), .data(out_7), .sel(in_4), .ld(in_6));  // open: clr
endmodule
